// Logisim project project2-devices.circ as structural Verilog: 2 circuits, main circuit Timer Device
module Timer_Device (
  input  Clock,
  input  IntAck,
  input  [31:0] Limit,
  input  [31:0] ID_In,
  output Int,
  output [31:0] ID_Out,
  output AckChain
);

  wire and_2_out, button_1_out, comparator_1_eq, comparator_1_gt, IntRaise, not_1_out, or_1_out;
  wire [31:0] Timer_q;

  Pull_Resistor pull_resistor_1 (.node(IntAck));
  assign Int = IntRaise ? 1'b1 : 1'bz;  // Controlled_Buffer controlled_buffer_1
  and and_1 (AckChain, IntAck, ~IntRaise);  // AND_Gate
  not not_1 (not_1_out, IntAck);
  Counter #(.width(32), .max('hffffffff), .ongoal("stay")) Timer (
    .load(IntAck), .D({32{1'b0}}), .count(not_1_out), .Q(Timer_q), .clk(Clock), .clr(button_1_out));  // open: carry
  Button button_1 (.out(button_1_out));
  assign ID_Out = IntAck ? ID_In : 32'bz;  // Controlled_Buffer controlled_buffer_2
  or or_1 (or_1_out, comparator_1_gt, comparator_1_eq);
  Comparator #(.width(32), .mode("unsigned")) comparator_1 (
    .a(Timer_q), .b(Limit), .gt(comparator_1_gt), .eq(comparator_1_eq));  // open: lt
  and and_2 (and_2_out, or_1_out, ~IntAck);  // AND_Gate
  D_Flip_Flop d_ff_1 (.clk(Clock), .D(and_2_out), .Q(IntRaise));  // open: Qn, preset, en, reset

  // Other names for the same wires on the sheet: DeviceID[31:0] = ID_In

  // Notes on the sheet:
  //   Clear Button
endmodule

module Priority_Fence (
  input  INTIn,
  input  PriIn,
  input  INTAIn,
  input  PriClr,
  input  Clock,
  output INTOut
);

  wire and_3_out, and_4_out, INT0, INT1, INTA0, INTA1, not_1_out, not_2_out, Pri0, Pri1;
  wire [1:0] PriOut;

  and and_1 (INTA0, INTAIn, INT0);
  and and_2 (INTA1, INTAIn, INT1);
  and and_3 (and_3_out, INT1, ~PriOut[0], ~PriOut[1]);  // AND_Gate
  Register #(.width(2)) Priority_Register (.D({Pri1, Pri0}), .Q(PriOut), .clk(Clock));  // open: en, clr
  // Probe on PriOut
  not not_1 (not_1_out, PriClr);
  not not_2 (not_2_out, PriClr);
  and and_4 (and_4_out, INT0, ~PriOut[0]);  // AND_Gate
  Multiplexer #(.disabled(0), .enable("false")) multiplexer_1 (
    .in0(INTA0), .in1(not_1_out), .out(Pri0), .sel(PriOut[0]));
  Multiplexer #(.select(2), .disabled(0), .enable("false")) multiplexer_2 (
    .in0(INTA1), .in1(1'b0), .in2(not_2_out), .in3(1'b1), .out(Pri1), .sel(PriOut));
  or or_1 (INTOut, and_4_out, and_3_out);
  and and_5 (INT0, INTIn, ~PriIn);  // AND_Gate
  and and_6 (INT1, INTIn, PriIn);
endmodule
